// Logisim project minimized-build.circ as structural Verilog: 1 circuit, main circuit main
module main (
  input  A,
  input  B,
  input  C,
  input  D,
  output X
);

  wire and_1_out, and_2_out, and_3_out, and_4_out, not_1_out, not_2_out, not_3_out, not_4_out, or_1_out;

  not not_1 (not_1_out, A);
  and and_1 (and_1_out, not_1_out, not_2_out);
  not not_2 (not_2_out, C);
  not not_3 (not_3_out, D);
  not not_4 (not_4_out, B);
  and and_2 (and_2_out, and_1_out, not_3_out);
  and and_3 (and_3_out, not_4_out, C);
  or or_1 (or_1_out, and_2_out, and_3_out);
  and and_4 (and_4_out, B, D);
  or or_2 (X, or_1_out, and_4_out);
endmodule
