// Logisim project TwoBitFullAdderCircuit.circ as structural Verilog: 1 circuit, main circuit main
module main (
  input  A,
  input  B,
  input  C,
  input  D,
  output S0,
  output S1,
  output C1
);

  wire and_1_out, and_2_out, and_3_out, xor_1_out;

  and and_1 (and_1_out, A, B);
  xor xor_1 (xor_1_out, C, D);
  and and_2 (and_2_out, C, D);
  xor xor_2 (S0, A, B);
  xor xor_3 (S1, and_1_out, xor_1_out);
  and and_3 (and_3_out, and_1_out, xor_1_out);
  or or_1 (C1, and_3_out, and_2_out);
endmodule
